# Fritzing sketch AutoBrightness (saved by Fritzing 0.9.2b)
breadboards: 1

parts:
  Arduino_Uno_(Rev3) = Arduino Uno (Rev3)
  R2 = Resistor [tolerance=±5% resistance=10k package="0402 [SMD]"]
  R3 = Photocell (LDR) [package=THT]

nets:
  N1: Arduino_Uno_(Rev3).A0, R2.Pin_0, R3.pin_0
  N2: Arduino_Uno_(Rev3).5V, R3.pin_1
  N3: Arduino_Uno_(Rev3).GND, R2.Pin_1
